// Logisim project rcd.circ as structural Verilog: 1 circuit, main circuit main
module main (
);

  wire and_3_out, and_6_out, and_7_out, and_16_out, and_17_out, and_18_out, and_25_out, and_30_out,
       and_31_out, clock_1_out, not_1_out, not_2_out, not_3_out, not_4_out, not_5_out, not_6_out, not_7_out,
       not_8_out, not_9_out, not_10_out, not_11_out, not_12_out, or_1_out, or_2_out, or_3_out, or_4_out;
  wire [1:0] rom_1_data_2;
  wire [3:0] and_9_out, and_11_out, and_21_out, and_22_out, and_32_out, and_33_out, rom_1_data_3,
       rom_1_data_4, undriven, undriven_2;
  wire [7:0] controlled_buffer_1_out, controlled_buffer_3_out, controlled_buffer_5_out, counter_1_q,
       ram_1_data, ram_2_data, ram_3_data, undriven_3, undriven_4, undriven_5;
  wire [9:0] rom_1_data, rom_1_data_5;

  Clock clock_1 (.out(clock_1_out));
  Counter counter_1 (.Q(counter_1_q), .clk(clock_1_out));  // open: load, D, count, carry, clr
  ROM #(.dataWidth(30)) rom_1 (
    .addr(counter_1_q), .data({rom_1_data_5, rom_1_data_2, rom_1_data_3, rom_1_data_4, rom_1_data}));  // open: sel
  or or_1 (or_1_out, undriven[3], undriven_2[3]);
  and and_1 (and_9_out[3], and_3_out, rom_1_data[7]);
  and and_2 (and_11_out[3], and_3_out, rom_1_data[3]);
  and and_3 (and_3_out, rom_1_data[8], rom_1_data[9]);
  not not_1 (not_1_out, rom_1_data[9]);
  not not_2 (not_2_out, rom_1_data[8]);
  or or_2 (or_2_out, undriven[2], undriven_2[2]);
  and and_4 (and_9_out[2], and_3_out, rom_1_data[6]);
  and and_5 (and_11_out[2], and_3_out, rom_1_data[2]);
  RAM #(.addrWidth(4)) ram_1 (
    .addr(rom_1_data[3:0]), .data(ram_1_data), .sel(1'b1), .clk(not_4_out), .ld(not_3_out), .clr(1'b0));
  not not_3 (not_3_out, and_7_out);
  not not_4 (not_4_out, clock_1_out);
  and and_6 (and_6_out, rom_1_data[8], not_1_out);
  and and_7 (and_7_out, not_2_out, rom_1_data[9]);
  or or_3 (or_3_out, undriven[0], undriven_2[0]);
  or or_4 (or_4_out, undriven[1], undriven_2[1]);
  and and_8 (and_9_out[1], and_3_out, rom_1_data[5]);
  and and_9 (and_9_out[0], and_3_out, rom_1_data[4]);
  and and_10 (and_11_out[1], and_3_out, rom_1_data[1]);
  and and_11 (and_11_out[0], and_3_out, rom_1_data[0]);
  assign controlled_buffer_1_out = and_6_out ? ram_1_data : 8'bz;  // Controlled_Buffer controlled_buffer_1
  assign ram_1_data = and_7_out ? undriven_3 : 8'bz;  // Controlled_Buffer controlled_buffer_2
  not not_5 (not_5_out, rom_1_data_2[1]);
  not not_6 (not_6_out, rom_1_data_2[0]);
  and and_12 (and_21_out[2], and_16_out, rom_1_data_3[2]);
  and and_13 (and_21_out[3], and_16_out, rom_1_data_3[3]);
  and and_14 (and_22_out[3], and_16_out, rom_1_data_4[3]);
  and and_15 (and_22_out[2], and_16_out, rom_1_data_4[2]);
  not not_7 (not_7_out, and_18_out);
  not not_8 (not_8_out, clock_1_out);
  and and_16 (and_16_out, rom_1_data_2[0], rom_1_data_2[1]);
  and and_17 (and_17_out, rom_1_data_2[0], not_5_out);
  and and_18 (and_18_out, not_6_out, rom_1_data_2[1]);
  and and_19 (and_21_out[1], and_16_out, rom_1_data_3[1]);
  and and_20 (and_22_out[1], and_16_out, rom_1_data_4[1]);
  assign controlled_buffer_3_out = and_17_out ? ram_2_data : 8'bz;  // Controlled_Buffer controlled_buffer_3
  RAM #(.addrWidth(4)) ram_2 (
    .addr(rom_1_data_4), .data(ram_2_data), .sel(1'b1), .clk(not_8_out), .ld(not_7_out), .clr(1'b0));
  assign ram_2_data = and_18_out ? undriven_4 : 8'bz;  // Controlled_Buffer controlled_buffer_4
  and and_21 (and_21_out[0], and_16_out, rom_1_data_3[0]);
  and and_22 (and_22_out[0], and_16_out, rom_1_data_4[0]);
  and and_23 (and_32_out[3], and_25_out, rom_1_data_5[7]);
  and and_24 (and_33_out[3], and_25_out, rom_1_data_5[3]);
  not not_9 (not_9_out, clock_1_out);
  and and_25 (and_25_out, rom_1_data_5[8], rom_1_data_5[9]);
  not not_10 (not_10_out, rom_1_data_5[9]);
  not not_11 (not_11_out, rom_1_data_5[8]);
  and and_26 (and_32_out[2], and_25_out, rom_1_data_5[6]);
  and and_27 (and_32_out[1], and_25_out, rom_1_data_5[5]);
  and and_28 (and_33_out[2], and_25_out, rom_1_data_5[2]);
  and and_29 (and_33_out[1], and_25_out, rom_1_data_5[1]);
  RAM #(.addrWidth(4)) ram_3 (
    .addr(rom_1_data_5[3:0]), .data(ram_3_data), .sel(1'b1), .clk(not_9_out), .ld(not_12_out), .clr(1'b0));
  not not_12 (not_12_out, and_31_out);
  and and_30 (and_30_out, rom_1_data_5[8], not_10_out);
  and and_31 (and_31_out, not_11_out, rom_1_data_5[9]);
  and and_32 (and_32_out[0], and_25_out, rom_1_data_5[4]);
  and and_33 (and_33_out[0], and_25_out, rom_1_data_5[0]);
  assign controlled_buffer_5_out = and_30_out ? ram_3_data : 8'bz;  // Controlled_Buffer controlled_buffer_5
  assign ram_3_data = and_31_out ? undriven_5 : 8'bz;  // Controlled_Buffer controlled_buffer_6
endmodule
